# Fritzing sketch SmartDumpster (saved by Fritzing 0.9.3b)
breadboards: 2

parts:
  U1 = ESP8266 NodeMCU LoLin module
  Part1 = Arduino Uno (Rev3)
  Part2 = Bluetooth HC-05 Macho
  LED2 = smd LED [color="Green (570nm)" package="0805 [SMD]"]
  R1 = Rotary Potentiometer (Small) [maximum_resistance=100kΩ package=THT]
  R2 = Resistor [tolerance=±5% resistance=1k package="2512 [SMD]"]
  R3 = Resistor [tolerance=±5% resistance=1k package="2512 [SMD]"]
  R4 = Resistor [tolerance=±5% resistance=220 package="2512 [SMD]"]
  R5 = Resistor [tolerance=±5% resistance=220 package="2512 [SMD]"]
  R6 = Resistor [tolerance=±5% resistance=220 package="2512 [SMD]"]
  LED1 = smd LED [color="Green (570nm)" package="0805 [SMD]"]
  LED3 = smd LED [color="Green (570nm)" package="0805 [SMD]"]
  LED4 = smd LED [color="Red (660nm)" package="0805 [SMD]"]
  R7 = Resistor [tolerance=±5% resistance=1k package="2512 [SMD]"]
  R8 = Resistor [tolerance=±5% resistance=1k package="2512 [SMD]"]
  LED5 = smd LED [color="Green (570nm)" package="0805 [SMD]"]
  R9 = Resistor [tolerance=±5% resistance=1k package="2512 [SMD]"]
  J1 = Basic Servo

nets:
  N1: U1.D1, Part1.D5_PWM
  N2: U1.D2, Part1.D6_PWM
  N3: U1.D3, LED3.anode
  N4: U1.D4, LED4.anode
  GND: U1.GND, Part1.GND, Part2.GND, LED2.cathode, R1.leg1, R6.Pin_0, LED1.cathode, R7.Pin_0, R8.Pin_0, LED5.cathode, J1.gnd
  3V3: U1.3V3, Part1.3V3
  N5: Part1.D8, J1.pulse
  N6: Part1.D9_PWM, R2.Pin_1
  N7: Part1.D13/SCK, R3.Pin_1
  N8: Part1.A4/SDA, R9.Pin_1
  N9: Part1.D2, R4.Pin_1
  N10: Part1.D3_PWM, Part2.TXD
  VCC: Part1.5V, Part2.VCC, R1.leg2, J1.vcc
  N11: Part2.RXD, R4.Pin_0, R5.Pin_1
  N12: LED2.anode, R2.Pin_0
  N13: R3.Pin_0, LED1.anode
  N14: R5.Pin_0, R6.Pin_1
  N15: LED3.cathode, R7.Pin_1
  N16: LED4.cathode, R8.Pin_1
  N17: LED5.anode, R9.Pin_0

custom parts:
  ESP8266 NodeMCU LoLin module: ESP8266 based NodeMCU
